// Logisim project processor.circ as structural Verilog: 1 circuit, main circuit main
module main (
  input  in_1,
  input  [7:0] in_2,
  input  [3:0] in_3,
  output [7:0] out_4
);

  wire clock_1_out, decoder_1_out0, decoder_1_out1, decoder_1_out2, decoder_1_out3, decoder_1_out4,
       decoder_1_out5, decoder_1_out6, decoder_1_out7, decoder_1_out8, decoder_1_out9, decoder_1_out10,
       decoder_1_out11, decoder_1_out12, decoder_1_out13, decoder_1_out14, decoder_1_out15;

  Clock clock_1 (.out(clock_1_out));
  Register a (.D(in_2), .en(decoder_1_out0), .Q(out_4), .clk(clock_1_out), .clr(in_1));
  Register b (.D(in_2), .en(decoder_1_out1), .Q(out_4), .clk(clock_1_out), .clr(in_1));
  Register j (.D(in_2), .en(decoder_1_out9), .Q(out_4), .clk(clock_1_out), .clr(in_1));
  Register i (.D(in_2), .en(decoder_1_out8), .Q(out_4), .clk(clock_1_out), .clr(in_1));
  Register c (.D(in_2), .en(decoder_1_out2), .Q(out_4), .clk(clock_1_out), .clr(in_1));
  Register k (.D(in_2), .en(decoder_1_out10), .Q(out_4), .clk(clock_1_out), .clr(in_1));
  ROM rom_1 ();  // open: addr, data, sel
  Register d (.D(in_2), .en(decoder_1_out3), .Q(out_4), .clk(clock_1_out), .clr(in_1));
  Register l (.D(in_2), .en(decoder_1_out11), .Q(out_4), .clk(clock_1_out), .clr(in_1));
  Register e (.D(in_2), .en(decoder_1_out4), .Q(out_4), .clk(clock_1_out), .clr(in_1));
  Register m (.D(in_2), .en(decoder_1_out12), .Q(out_4), .clk(clock_1_out), .clr(in_1));
  Register f (.D(in_2), .en(decoder_1_out5), .Q(out_4), .clk(clock_1_out), .clr(in_1));
  Register n (.D(in_2), .en(decoder_1_out13), .Q(out_4), .clk(clock_1_out), .clr(in_1));
  Register g (.D(in_2), .en(decoder_1_out6), .Q(out_4), .clk(clock_1_out), .clr(in_1));
  Register o (.D(in_2), .en(decoder_1_out14), .Q(out_4), .clk(clock_1_out), .clr(in_1));
  Register h (.D(in_2), .en(decoder_1_out7), .Q(out_4), .clk(clock_1_out), .clr(in_1));
  Register flags (.D(in_2), .en(decoder_1_out15), .Q(out_4), .clk(clock_1_out), .clr(in_1));
  Decoder #(.select(4)) decoder_1 (
    .out0(decoder_1_out0), .out1(decoder_1_out1), .out2(decoder_1_out2), .out3(decoder_1_out3),
    .out4(decoder_1_out4), .out5(decoder_1_out5), .out6(decoder_1_out6), .out7(decoder_1_out7),
    .out8(decoder_1_out8), .out9(decoder_1_out9), .out10(decoder_1_out10), .out11(decoder_1_out11),
    .out12(decoder_1_out12), .out13(decoder_1_out13), .out14(decoder_1_out14), .out15(decoder_1_out15),
    .sel(in_3));  // open: en

  // Notes on the sheet:
  //   contents of rom_1 (hex, n*v repeats v):
  //   c1 10 c2 18 11 12 e1 80 0 a0 7
endmodule
